// Logisim project em_processo.circ as structural Verilog: 10 circuits, main circuit main
module main (
);

  wire CLK, down, left, read_mem, right, uc_w_1_alusrc, uc_w_1_jump, uc_w_1_regdest, uc_w_1_regwrite, up,
       wr_mem;
  wire [2:0] uc_w_1_aluop;
  wire [4:0] multiplexer_1_out;
  wire [5:0] alu_control_cdc02c58_1_out_3;
  wire [15:0] adder_1_out, address_in, multiplexer_3_out, PC_q, system_1_out_11, system_1_out_12,
       system_1_out_13, system_1_out_14, system_1_out_16, system_1_out_17, system_1_out_18, system_1_out_19,
       system_1_out_20, system_1_out_21, system_1_out_22, system_1_out_23, system_1_out_24, system_1_out_25,
       system_1_out_26, system_1_out_27;
  wire [31:0] banco_registradores_7e917d75_1_r1, bit_extender_1_out, data_mem, DATA_MEMORY_fd7e8c3a_dout,
       data_out, data_write, INSTRUCTION_MEMORY_dd550cf9_dout, multiplexer_2_out, ula_1_resultado;

  Register #(.trigger("high"), .width(16)) PC (.D(multiplexer_3_out), .Q(PC_q), .clk(CLK));  // open: en, clr
  Clock clock_1 (.out(CLK));
  Adder #(.width(16)) adder_1 (.a(16'h1), .b(PC_q), .out(adder_1_out));  // open: cin, cout
  RAM #(.addrWidth(16), .dataWidth(32)) INSTRUCTION_MEMORY_dd550cf9 (
    .addr(PC_q), .clk(CLK), .dout(INSTRUCTION_MEMORY_dd550cf9_dout));  // open: we, oe, din
  UC_W uc_w_1 (
    .in_1(INSTRUCTION_MEMORY_dd550cf9_dout[31:26]), .JUMP(uc_w_1_jump), .MEMTOREG(read_mem),
    .ALUSRC(uc_w_1_alusrc), .REGWRITE(uc_w_1_regwrite), .ALUOP(uc_w_1_aluop), .MEMWRITE(wr_mem),
    .REGDEST(uc_w_1_regdest));  // open: BRANCH
  Multiplexer #(.width(5)) multiplexer_1 (
    .in0(INSTRUCTION_MEMORY_dd550cf9_dout[20:16]), .in1(INSTRUCTION_MEMORY_dd550cf9_dout[15:11]),
    .out(multiplexer_1_out), .sel(uc_w_1_regdest));
  banco_registradores_7e917d75 banco_registradores_7e917d75_1 (
    .RW(multiplexer_1_out), .Din(data_out), .WE(uc_w_1_regwrite), .clk(CLK),
    .R1Z(INSTRUCTION_MEMORY_dd550cf9_dout[25:21]), .R2Z(INSTRUCTION_MEMORY_dd550cf9_dout[20:16]),
    .R2(data_write), .R1(banco_registradores_7e917d75_1_r1));
  SYSTEM system_1 (
    .DATA_OUT(data_out), .ADDRESS_IN(address_in), .wr_mem(wr_mem), .DATA_WR(data_write), .LEFT(left),
    .DOWN(down), .RIGHT(right), .UP(up), .DATA_MEM(data_mem), .CLK(CLK), .MEM_READ(read_mem),
    .out_11(system_1_out_11), .out_12(system_1_out_12), .out_13(system_1_out_13), .out_14(system_1_out_14),
    .out_16(system_1_out_16), .out_17(system_1_out_17), .out_18(system_1_out_18), .out_19(system_1_out_19),
    .out_20(system_1_out_20), .out_21(system_1_out_21), .out_22(system_1_out_22), .out_23(system_1_out_23),
    .out_24(system_1_out_24), .out_25(system_1_out_25), .out_26(system_1_out_26), .out_27(system_1_out_27));
  DotMatrix #(.inputtype("row"), .matrixcols(16), .matrixrows(16)) dotmatrix_1 (
    .row0(system_1_out_11), .row1(system_1_out_12), .row2(system_1_out_13), .row3(system_1_out_14),
    .row4(system_1_out_16), .row5(system_1_out_17), .row6(system_1_out_18), .row7(system_1_out_19),
    .row8(system_1_out_20), .row9(system_1_out_21), .row10(system_1_out_22), .row11(system_1_out_23),
    .row12(system_1_out_24), .row13(system_1_out_25), .row14(system_1_out_26), .row15(system_1_out_27));
  Button button_1 (.out(left));
  assign bit_extender_1_out = {{16{INSTRUCTION_MEMORY_dd550cf9_dout[15]}}, INSTRUCTION_MEMORY_dd550cf9_dout[15:0]};  // Bit_Extender bit_extender_1
  ALU_CONTROL_cdc02c58 alu_control_cdc02c58_1 (
    .in_1(INSTRUCTION_MEMORY_dd550cf9_dout[5:0]), .in_2(uc_w_1_aluop), .out_3(alu_control_cdc02c58_1_out_3));
  Button button_2 (.out(up));
  Button button_3 (.out(right));
  Button button_4 (.out(down));
  ULA ula_1 (
    .A(banco_registradores_7e917d75_1_r1), .B(multiplexer_2_out), .OP(alu_control_cdc02c58_1_out_3),
    .Resultado(ula_1_resultado));  // open: igual, menor
  Multiplexer #(.width(32)) multiplexer_2 (
    .in0(data_write), .in1(bit_extender_1_out), .out(multiplexer_2_out), .sel(uc_w_1_alusrc));
  Multiplexer #(.width(16)) multiplexer_3 (
    .in0(adder_1_out), .in1(INSTRUCTION_MEMORY_dd550cf9_dout[15:0]), .out(multiplexer_3_out),
    .sel(uc_w_1_jump));
  Bit_Extender #(.in_width(32)) bit_extender_2 (.in(ula_1_resultado), .out(address_in));
  RAM #(.addrWidth(16), .dataWidth(32)) DATA_MEMORY_fd7e8c3a (
    .addr(address_in), .we(wr_mem), .clk(CLK), .din(data_write), .dout(DATA_MEMORY_fd7e8c3a_dout));  // open: oe
  Multiplexer #(.width(32)) multiplexer_4 (
    .in0(ula_1_resultado), .in1(DATA_MEMORY_fd7e8c3a_dout), .out(data_mem), .sel(read_mem));

  // Notes on the sheet:
  //   RegDest
  //   Jump
  //   Branch
  //   MenToReg
  //   ALUOp
  //   MemWrite
  //   AluSRC
  //   RegWrite
endmodule

module banco_registradores_7e917d75 (
  input  [4:0] R1Z,
  input  [4:0] R2Z,
  input  [4:0] RW,
  input  [31:0] Din,
  input  WE,
  input  clk,
  output [31:0] R1,
  output [31:0] R2
);

  wire demultiplexer_1_out0, demultiplexer_1_out1, demultiplexer_1_out2, demultiplexer_1_out3,
       demultiplexer_2_out0, demultiplexer_2_out1, demultiplexer_2_out2, demultiplexer_2_out3,
       demultiplexer_2_out4, demultiplexer_2_out5, demultiplexer_2_out6, demultiplexer_2_out7,
       demultiplexer_3_out0, demultiplexer_3_out1, demultiplexer_3_out2, demultiplexer_3_out3,
       demultiplexer_3_out4, demultiplexer_3_out5, demultiplexer_3_out6, demultiplexer_3_out7,
       demultiplexer_4_out0, demultiplexer_4_out1, demultiplexer_4_out2, demultiplexer_4_out3,
       demultiplexer_4_out4, demultiplexer_4_out5, demultiplexer_4_out6, demultiplexer_4_out7,
       demultiplexer_5_out0, demultiplexer_5_out1, demultiplexer_5_out2, demultiplexer_5_out3,
       demultiplexer_5_out4, demultiplexer_5_out5, demultiplexer_5_out6, demultiplexer_5_out7;
  wire [4:0] reg1_b1a1e9b0, reg2_d573a5ce, write_reg_c415683c;
  wire [31:0] a0, a1_5_q, a2_6_q, a3_7_q, at_1_q, k0_26_q, L_27_k1_9a6d92d3_q, L_28_gp_c2c87104_q,
       L_29_sp_6d44a2e9_q, L_30_fp_b08d7dab_q, L_ra_11c22e28, s0, s1, s2, s3_19_q, s4_20_q, s5_21_q, s6_22_q,
       s7_23_q, t0_8_q, t1_9_q, t2_10_q, t3_11_q, t4_12_q, t5_12_p4, t6_14_q, t7_15_q, t8_24_q, t9_25_q, v0,
       v1_3_q, Zero_0_q;

  Demultiplexer #(.select(2)) demultiplexer_1 (
    .out0(demultiplexer_1_out0), .out1(demultiplexer_1_out1), .out2(demultiplexer_1_out2),
    .out3(demultiplexer_1_out3), .in(1'b1), .sel(write_reg_c415683c[4:3]));
  Demultiplexer #(.select(3)) demultiplexer_2 (
    .out0(demultiplexer_2_out0), .out1(demultiplexer_2_out1), .out2(demultiplexer_2_out2),
    .out3(demultiplexer_2_out3), .out4(demultiplexer_2_out4), .out5(demultiplexer_2_out5),
    .out6(demultiplexer_2_out6), .out7(demultiplexer_2_out7), .in(1'b1), .sel(write_reg_c415683c[2:0]));
  Demultiplexer #(.select(3)) demultiplexer_3 (
    .out0(demultiplexer_3_out0), .out1(demultiplexer_3_out1), .out2(demultiplexer_3_out2),
    .out3(demultiplexer_3_out3), .out4(demultiplexer_3_out4), .out5(demultiplexer_3_out5),
    .out6(demultiplexer_3_out6), .out7(demultiplexer_3_out7), .in(1'b1), .sel(write_reg_c415683c[2:0]));
  Demultiplexer #(.select(3)) demultiplexer_4 (
    .out0(demultiplexer_4_out0), .out1(demultiplexer_4_out1), .out2(demultiplexer_4_out2),
    .out3(demultiplexer_4_out3), .out4(demultiplexer_4_out4), .out5(demultiplexer_4_out5),
    .out6(demultiplexer_4_out6), .out7(demultiplexer_4_out7), .in(1'b1), .sel(write_reg_c415683c[2:0]));
  Demultiplexer #(.select(3)) demultiplexer_5 (
    .out0(demultiplexer_5_out0), .out1(demultiplexer_5_out1), .out2(demultiplexer_5_out2),
    .out3(demultiplexer_5_out3), .out4(demultiplexer_5_out4), .out5(demultiplexer_5_out5),
    .out6(demultiplexer_5_out6), .out7(demultiplexer_5_out7), .in(1'b1), .sel(write_reg_c415683c[2:0]));
  Register #(.trigger("high"), .width(32)) Zero_0 (.D(Din), .en(demultiplexer_2_out0), .Q(Zero_0_q));  // open: clk, clr
  Register #(.trigger("high"), .width(32)) t0_8 (
    .D(Din), .en(demultiplexer_3_out0), .Q(t0_8_q), .clk(clk));  // open: clr
  Register #(.trigger("high"), .width(32)) s0_16 (.D(Din), .en(demultiplexer_4_out0), .Q(s0), .clk(clk));  // open: clr
  Register #(.trigger("high"), .width(32)) t8_24 (
    .D(Din), .en(demultiplexer_5_out0), .Q(t8_24_q), .clk(clk));  // open: clr
  Register #(.trigger("high"), .width(32)) at_1 (
    .D(Din), .en(demultiplexer_2_out1), .Q(at_1_q), .clk(clk));  // open: clr
  Register #(.trigger("high"), .width(32)) t1_9 (
    .D(Din), .en(demultiplexer_3_out1), .Q(t1_9_q), .clk(clk));  // open: clr
  Register #(.trigger("high"), .width(32)) s1_17 (.D(Din), .en(demultiplexer_4_out1), .Q(s1), .clk(clk));  // open: clr
  Register #(.trigger("high"), .width(32)) t9_25 (
    .D(Din), .en(demultiplexer_5_out1), .Q(t9_25_q), .clk(clk));  // open: clr
  Register #(.trigger("high"), .width(32)) v0_2 (.D(Din), .en(demultiplexer_2_out2), .Q(v0), .clk(clk));  // open: clr
  Register #(.trigger("high"), .width(32)) t2_10 (
    .D(Din), .en(demultiplexer_3_out2), .Q(t2_10_q), .clk(clk));  // open: clr
  Register #(.trigger("high"), .width(32)) s2_18 (.D(Din), .en(demultiplexer_4_out2), .Q(s2), .clk(clk));  // open: clr
  Register #(.trigger("high"), .width(32)) k0_26 (
    .D(Din), .en(demultiplexer_5_out2), .Q(k0_26_q), .clk(clk));  // open: clr
  Register #(.trigger("high"), .width(32)) v1_3 (
    .D(Din), .en(demultiplexer_2_out3), .Q(v1_3_q), .clk(clk));  // open: clr
  Register #(.trigger("high"), .width(32)) t3_11 (
    .D(Din), .en(demultiplexer_3_out3), .Q(t3_11_q), .clk(clk));  // open: clr
  Register #(.trigger("high"), .width(32)) s3_19 (
    .D(Din), .en(demultiplexer_4_out3), .Q(s3_19_q), .clk(clk));  // open: clr
  Register #(.trigger("high"), .width(32)) L_27_k1_9a6d92d3 (
    .D(Din), .en(demultiplexer_5_out3), .Q(L_27_k1_9a6d92d3_q), .clk(clk));  // open: clr
  Register #(.trigger("high"), .width(32)) a0_4 (.D(Din), .en(demultiplexer_2_out4), .Q(a0), .clk(clk));  // open: clr
  Register #(.trigger("high"), .width(32)) t4_12 (
    .D(Din), .en(demultiplexer_3_out4), .Q(t4_12_q), .clk(clk));  // open: clr
  Register #(.trigger("high"), .width(32)) s4_20 (
    .D(Din), .en(demultiplexer_4_out4), .Q(s4_20_q), .clk(clk));  // open: clr
  Register #(.trigger("high"), .width(32)) L_28_gp_c2c87104 (
    .D(Din), .en(demultiplexer_5_out4), .Q(L_28_gp_c2c87104_q), .clk(clk));  // open: clr
  Register #(.trigger("high"), .width(32)) a1_5 (
    .D(Din), .en(demultiplexer_2_out5), .Q(a1_5_q), .clk(clk));  // open: clr
  // Register #(.trigger("high"), .width(32)) t5_12: pin names not known; wires that end beside it: Din, demultiplexer_3_out5, clk, t5_12_p4
  Register #(.trigger("high"), .width(32)) s5_21 (
    .D(Din), .en(demultiplexer_4_out5), .Q(s5_21_q), .clk(clk));  // open: clr
  Register #(.trigger("high"), .width(32)) L_29_sp_6d44a2e9 (
    .D(Din), .en(demultiplexer_5_out5), .Q(L_29_sp_6d44a2e9_q), .clk(clk));  // open: clr
  Register #(.trigger("high"), .width(32)) a2_6 (
    .D(Din), .en(demultiplexer_2_out6), .Q(a2_6_q), .clk(clk));  // open: clr
  Register #(.trigger("high"), .width(32)) t6_14 (
    .D(Din), .en(demultiplexer_3_out6), .Q(t6_14_q), .clk(clk));  // open: clr
  Register #(.trigger("high"), .width(32)) s6_22 (
    .D(Din), .en(demultiplexer_4_out6), .Q(s6_22_q), .clk(clk));  // open: clr
  Register #(.trigger("high"), .width(32)) L_30_fp_b08d7dab (
    .D(Din), .en(demultiplexer_5_out6), .Q(L_30_fp_b08d7dab_q), .clk(clk));  // open: clr
  Register #(.trigger("high"), .width(32)) a3_7 (
    .D(Din), .en(demultiplexer_2_out7), .Q(a3_7_q), .clk(clk));  // open: clr
  Register #(.trigger("high"), .width(32)) t7_15 (
    .D(Din), .en(demultiplexer_3_out7), .Q(t7_15_q), .clk(clk));  // open: clr
  Register #(.trigger("high"), .width(32)) s7_23 (
    .D(Din), .en(demultiplexer_4_out7), .Q(s7_23_q), .clk(clk));  // open: clr
  Register #(.trigger("high"), .width(32)) L_31_ra_3db83422 (
    .D(Din), .en(demultiplexer_5_out7), .Q(L_ra_11c22e28), .clk(clk));  // open: clr
  Multiplexer #(.select(5), .width(32)) multiplexer_1 (
    .in0(Zero_0_q), .in1(at_1_q), .in2(v0), .in3(v1_3_q), .in4(a0), .in5(a1_5_q), .in6(a2_6_q), .in7(a3_7_q),
    .in8(t0_8_q), .in9(t1_9_q), .in10(t2_10_q), .in11(t3_11_q), .in12(t4_12_q), .in13(t5_12_p4),
    .in14(t6_14_q), .in15(t7_15_q), .in16(s0), .in17(s1), .in18(s2), .in19(s3_19_q), .in20(s4_20_q),
    .in21(s5_21_q), .in22(s6_22_q), .in23(s7_23_q), .in24(t8_24_q), .in25(t9_25_q), .in26(k0_26_q),
    .in27(L_27_k1_9a6d92d3_q), .in28(L_28_gp_c2c87104_q), .in29(L_29_sp_6d44a2e9_q),
    .in30(L_30_fp_b08d7dab_q), .in31(L_ra_11c22e28), .out(R1), .sel(reg1_b1a1e9b0));
  Multiplexer #(.select(5), .width(32)) multiplexer_2 (
    .in0(Zero_0_q), .in1(at_1_q), .in2(v0), .in3(v1_3_q), .in4(a0), .in5(a1_5_q), .in6(a2_6_q), .in7(a3_7_q),
    .in8(t0_8_q), .in9(t1_9_q), .in10(t2_10_q), .in11(t3_11_q), .in12(t4_12_q), .in13(t5_12_p4),
    .in14(t6_14_q), .in15(t7_15_q), .in16(s0), .in17(s1), .in18(s2), .in19(s3_19_q), .in20(s4_20_q),
    .in21(s5_21_q), .in22(s6_22_q), .in23(s7_23_q), .in24(t8_24_q), .in25(t9_25_q), .in26(k0_26_q),
    .in27(L_27_k1_9a6d92d3_q), .in28(L_28_gp_c2c87104_q), .in29(L_29_sp_6d44a2e9_q),
    .in30(L_30_fp_b08d7dab_q), .in31(L_ra_11c22e28), .out(R2), .sel(reg2_d573a5ce));

  // Other names for the same wires on the sheet: reg1[31:0] = R1; reg1Z[4:0] = R1Z; reg2[31:0] = R2; reg2Z[4:0] = R2Z;
  //   write_data[31:0] = Din; write_regZ[4:0] = RW

  // Notes on the sheet:
  //   Input
  //   Output
endmodule

module ULA (
  input  [31:0] A,
  input  [31:0] B,
  input  [5:0] OP,
  output igual,
  output menor,
  output [31:0] Resultado
);

  wire [31:0] adder_1_out, divider_1_out, multiplier_1_out, subtractor_1_out;

  Adder #(.width(32)) adder_1 (.a(A), .b(B), .out(adder_1_out));  // open: cin, cout
  Subtractor #(.width(32)) subtractor_1 (.a(A), .b(B), .out(subtractor_1_out));  // open: bin, bout
  Multiplier #(.width(32)) multiplier_1 (.a(A), .b(B), .out(multiplier_1_out));  // open: cin, cout
  Divider #(.width(32)) divider_1 (.a(A), .b(B), .out(divider_1_out));  // open: upper, rem
  Comparator #(.width(32)) comparator_1 (.a(A), .b(B), .eq(igual), .lt(menor));  // open: gt
  Multiplexer #(.select(2), .width(32)) multiplexer_1 (
    .in0(adder_1_out), .in1(subtractor_1_out), .in2(multiplier_1_out), .in3(divider_1_out), .out(Resultado),
    .sel(OP[1:0]));
endmodule

module UC (
  input  UC5,
  input  UC4,
  input  UC3,
  input  UC2,
  input  UC1,
  input  UC0,
  output REGDEST,
  output JUMP,
  output BRANCH,
  output MEMTOREG,
  output ULA0P1,
  output ULA0P0,
  output ULAOPSRC,
  output MEM_WR,
  output ULASRC,
  output WR
);

  wire and_2_out, and_3_out, and_4_out, and_5_out, and_8_out, and_9_out, and_10_out, and_11_out, and_12_out,
       and_13_out, and_14_out, and_15_out, and_16_out, and_17_out, and_18_out, and_19_out, and_20_out,
       and_21_out, and_22_out, and_23_out, and_24_out, and_25_out, and_26_out, and_27_out, and_28_out,
       and_29_out, and_30_out, and_31_out, and_32_out, and_33_out, and_34_out, and_35_out, and_36_out,
       not_1_out, not_2_out, not_3_out, not_4_out, not_5_out, not_6_out, not_7_out, not_8_out, not_9_out,
       not_10_out, not_11_out, not_12_out, not_13_out, not_14_out, not_15_out, not_16_out, not_17_out,
       not_18_out, not_19_out, not_20_out, not_21_out, not_22_out, not_23_out, not_24_out, not_25_out,
       not_26_out, not_27_out, not_28_out, not_29_out, not_30_out, not_31_out, not_32_out, not_33_out,
       not_34_out, not_35_out, not_36_out, not_37_out, not_38_out, not_39_out, not_40_out, not_41_out,
       not_42_out, not_43_out, not_44_out, not_45_out, or_8_out;

  not not_1 (not_1_out, UC0);
  not not_2 (not_2_out, UC0);
  not not_3 (not_3_out, UC0);
  not not_4 (not_4_out, UC5);
  not not_5 (not_5_out, UC4);
  not not_6 (not_6_out, UC0);
  not not_7 (not_7_out, UC0);
  not not_8 (not_8_out, UC5);
  not not_9 (not_9_out, UC4);
  not not_10 (not_10_out, UC0);
  not not_11 (not_11_out, UC0);
  and and_1 (MEMTOREG, UC0, UC0);
  not not_12 (not_12_out, UC0);
  not not_13 (not_13_out, UC0);
  not not_14 (not_14_out, UC0);
  not not_15 (not_15_out, UC0);
  not not_16 (not_16_out, UC0);
  not not_17 (not_17_out, UC0);
  not not_18 (not_18_out, UC0);
  not not_19 (not_19_out, UC0);
  or or_1 (ULAOPSRC, UC0, UC0, UC0, UC0);
  not not_20 (not_20_out, UC5);
  not not_21 (not_21_out, UC4);
  not not_22 (not_22_out, UC0);
  not not_23 (not_23_out, UC0);
  not not_24 (not_24_out, UC0);
  not not_25 (not_25_out, UC0);
  not not_26 (not_26_out, UC5);
  not not_27 (not_27_out, UC4);
  not not_28 (not_28_out, UC0);
  not not_29 (not_29_out, UC0);
  not not_30 (not_30_out, UC5);
  not not_31 (not_31_out, UC4);
  not not_32 (not_32_out, UC0);
  not not_33 (not_33_out, UC0);
  not not_34 (not_34_out, UC5);
  not not_35 (not_35_out, UC4);
  not not_36 (not_36_out, UC0);
  not not_37 (not_37_out, UC0);
  not not_38 (not_38_out, UC5);
  not not_39 (not_39_out, UC4);
  not not_40 (not_40_out, UC0);
  not not_41 (not_41_out, UC0);
  not not_42 (not_42_out, UC0);
  not not_43 (not_43_out, UC0);
  not not_44 (not_44_out, UC0);
  not not_45 (not_45_out, UC0);
  and and_2 (and_2_out, UC0, UC0, UC0);
  and and_3 (and_3_out, UC0, UC0);
  and and_4 (and_4_out, not_1_out, not_2_out, not_3_out);
  and and_5 (and_5_out, UC0, UC0);
  and and_6 (JUMP, not_4_out, not_5_out, UC0, not_6_out, not_7_out);
  and and_7 (BRANCH, not_8_out, not_9_out, not_10_out, UC0, not_11_out, UC0);
  and and_8 (and_8_out, not_12_out, UC0, UC0);
  and and_9 (and_9_out, UC0, not_13_out);
  and and_10 (and_10_out, not_14_out, UC0, not_15_out);
  and and_11 (and_11_out, UC0, not_16_out);
  and and_12 (and_12_out, UC0, UC0, not_17_out);
  and and_13 (and_13_out, UC4, UC0, not_18_out);
  and and_14 (and_14_out, UC5, UC0, not_19_out);
  and and_15 (and_15_out, not_20_out, not_21_out, UC0, UC0, UC0);
  and and_16 (and_16_out, UC0, UC0, UC0);
  and and_17 (and_17_out, UC0, UC0, UC0);
  and and_18 (and_18_out, UC4, UC0);
  and and_19 (and_19_out, UC5, UC0);
  and and_20 (and_20_out, not_22_out, not_23_out, UC0);
  and and_21 (and_21_out, not_24_out, UC0, not_25_out);
  and and_22 (and_22_out, UC0, UC0, UC0);
  and and_23 (and_23_out, UC4, UC0);
  and and_24 (and_24_out, UC4, UC0);
  and and_25 (and_25_out, UC5, UC0);
  and and_26 (and_26_out, UC5, UC0);
  and and_27 (and_27_out, not_26_out, not_27_out, not_28_out, not_29_out);
  and and_28 (and_28_out, not_30_out, not_31_out, not_32_out, not_33_out);
  and and_29 (and_29_out, not_34_out, not_35_out, not_36_out, not_37_out, UC0);
  and and_30 (and_30_out, not_38_out, not_39_out, not_40_out, UC0, not_41_out);
  and and_31 (and_31_out, UC0, not_42_out, not_43_out);
  and and_32 (and_32_out, UC0, not_44_out, UC0);
  and and_33 (and_33_out, UC0, UC0, UC0);
  and and_34 (and_34_out, UC4, UC0);
  and and_35 (and_35_out, UC5, UC0);
  and and_36 (and_36_out, UC0, UC0, not_45_out);
  or or_2 (REGDEST, and_4_out, and_5_out, UC0, UC4, UC5);
  or or_3 (ULA0P1, and_8_out, and_9_out);
  or or_4 (ULA0P0, and_10_out, and_11_out, and_12_out, and_13_out, and_14_out);
  or or_5 (MEM_WR, and_15_out, and_16_out, and_17_out, and_18_out, and_19_out);
  or or_6 (ULASRC, and_20_out, UC0, and_21_out, and_22_out, and_23_out, and_24_out, and_25_out, and_26_out);
  or or_7 (WR, and_27_out, and_28_out, and_29_out, and_30_out);
  or or_8 (or_8_out, and_31_out, and_32_out, and_33_out, and_34_out, and_35_out);

  assign UC1 = UC0;
  assign UC2 = UC0;
  assign UC3 = UC0;
endmodule

// ULAOP
module OPULA (
  input  OPCOD0,
  input  OPCOD1,
  input  OPCOD2,
  input  OPCOD3,
  input  OPCOD4,
  input  OPCOD5,
  input  FUNC0,
  input  FUNC1,
  input  FUNC2,
  input  FUNC3,
  input  FUNC4,
  input  FUNC5,
  output ULAOP0,
  output ULAOP1,
  output ULAOP2,
  output ULAOP3
);
endmodule

// ALUCONTROL
module ALU_CONTROL_cdc02c58 (
  input  [5:0] in_1,
  input  [2:0] in_2,
  output [5:0] out_3
);

  wire [5:0] bit_extender_1_out;

  assign bit_extender_1_out = {{4{in_2[1]}}, in_2[1:0]};  // Bit_Extender bit_extender_1
  Multiplexer #(.width(6)) multiplexer_1 (.in0(in_1), .in1(bit_extender_1_out), .out(out_3), .sel(in_2[2]));
endmodule

// UC
module UC_W (
  input  [5:0] in_1,
  output REGDEST,
  output JUMP,
  output BRANCH,
  output MEMTOREG,
  output [2:0] ALUOP,
  output MEMWRITE,
  output ALUSRC,
  output REGWRITE
);

  UC uc_1 (
    .UC3(in_1[3]), .UC2(in_1[2]), .UC1(in_1[1]), .UC0(in_1[0]), .UC5(in_1[5]), .UC4(in_1[4]),
    .MEM_WR(MEMWRITE), .ULASRC(ALUSRC), .REGDEST(REGDEST), .WR(REGWRITE), .JUMP(JUMP), .BRANCH(BRANCH),
    .MEMTOREG(MEMTOREG), .ULA0P1(ALUOP[1]), .ULA0P0(ALUOP[0]), .ULAOPSRC(ALUOP[2]));
endmodule

module matrix_wr (
  input  [15:0] address,
  input  wr,
  input  clk,
  input  data,
  output [7:0] row0,
  output [7:0] row1,
  output [7:0] row2,
  output [7:0] row3,
  output [7:0] row4,
  output [7:0] row5,
  output [7:0] row6,
  output [7:0] row7
);

  wire t0, t1, t2, t3, t4, t5, t6, t7;

  Decoder #(.select(3)) decoder_1 (
    .out0(t0), .out1(t1), .out2(t2), .out3(t3), .out4(t4), .out5(t5), .out6(t6), .out7(t7),
    .sel(address[5:3]), .en(wr));
  row row_1 (.data_in(data), .row_en(t0), .col(address[2:0]), .clk(clk), .out(row0));
  row row_2 (.data_in(data), .row_en(t1), .col(address[2:0]), .clk(clk), .out(row1));
  row row_3 (.data_in(data), .row_en(t2), .col(address[2:0]), .clk(clk), .out(row2));
  row row_4 (.data_in(data), .row_en(t3), .col(address[2:0]), .clk(clk), .out(row3));
  row row_5 (.data_in(data), .row_en(t4), .col(address[2:0]), .clk(clk), .out(row4));
  row row_6 (.data_in(data), .row_en(t5), .col(address[2:0]), .clk(clk), .out(row5));
  row row_7 (.data_in(data), .row_en(t6), .col(address[2:0]), .clk(clk), .out(row6));
  row row_8 (.data_in(data), .row_en(t7), .col(address[2:0]), .clk(clk), .out(row7));

  // Other names for the same wires on the sheet: col[2:0] = address[2:0]; data_in = data
endmodule

module row (
  input  data_in,
  input  row_en,
  input  [2:0] col,
  input  clk,
  output [7:0] out
);

  wire decoder_1_out0, decoder_1_out1, decoder_1_out2, decoder_1_out3, decoder_1_out4, decoder_1_out5,
       decoder_1_out6, decoder_1_out7;

  Decoder #(.select(3)) decoder_1 (
    .out0(decoder_1_out0), .out1(decoder_1_out1), .out2(decoder_1_out2), .out3(decoder_1_out3),
    .out4(decoder_1_out4), .out5(decoder_1_out5), .out6(decoder_1_out6), .out7(decoder_1_out7), .sel(col),
    .en(row_en));
  Register #(.trigger("high"), .width(1)) register_1 (.Q(out[3]), .clr(out[3]));  // open: D, en, clk
  Register #(.trigger("high"), .width(1)) register_2 (.clk(out[2]), .Q(out[6]), .clr(out[3]));  // open: D, en
  Register #(.trigger("high"), .width(1)) register_3 (.Q(out[6]), .clr(out[3]));  // open: D, en, clk
  Register #(.trigger("high"), .width(1)) register_4 (
    .D(data_in), .en(decoder_1_out3), .Q(out[3]), .clk(clk));  // open: clr
  Register #(.trigger("high"), .width(1)) register_5 (
    .D(data_in), .en(decoder_1_out4), .Q(out[4]), .clk(clk));  // open: clr
  Register #(.trigger("high"), .width(1)) register_6 (.clk(out[6]), .Q(out[6]));  // open: D, en, clr
  Register #(.trigger("high"), .width(1)) register_7 (
    .D(data_in), .en(decoder_1_out6), .Q(out[6]), .clk(clk));  // open: clr
  Register #(.trigger("high"), .width(1)) register_8 (
    .D(data_in), .en(decoder_1_out7), .Q(out[7]), .clk(clk));  // open: clr
endmodule

module SYSTEM (
  input  [31:0] DATA_MEM,
  input  MEM_READ,
  input  [15:0] ADDRESS_IN,
  input  wr_mem,
  input  [31:0] DATA_WR,
  input  LEFT,
  input  DOWN,
  input  RIGHT,
  input  UP,
  input  CLK,
  output [15:0] out_11,
  output [15:0] out_12,
  output [15:0] out_13,
  output [15:0] out_14,
  output [31:0] DATA_OUT,
  output [15:0] out_16,
  output [15:0] out_17,
  output [15:0] out_18,
  output [15:0] out_19,
  output [15:0] out_20,
  output [15:0] out_21,
  output [15:0] out_22,
  output [15:0] out_23,
  output [15:0] out_24,
  output [15:0] out_25,
  output [15:0] out_26,
  output [15:0] out_27
);

  wire and_1_out, and_2_out, and_3_out, and_4_out, and_5_out, and_6_out, bit_extender_1_out, comparator_1_eq,
       comparator_2_eq, comparator_3_eq, comparator_4_eq, comparator_5_eq, comparator_6_eq, d_ff_2_qn,
       d_ff_4_p3, or_1_out, or_2_out, or_3_out, or_4_out;
  wire [3:0] d_ff_1_p4, undriven;
  wire [31:0] bit_extender_2_out, bit_extender_3_out, keyboard, multiplexer_2_out;

  Comparator #(.width(16)) comparator_1 (.a(ADDRESS_IN), .b(16'hfefe), .eq(comparator_1_eq));  // open: gt, lt
  Multiplexer #(.width(32)) multiplexer_1 (
    .in0(multiplexer_2_out), .in1(bit_extender_2_out), .out(DATA_OUT), .sel(and_1_out));
  Random #(.width(4)) random_1 ();  // open: clr, next, clk, out
  Bit_Extender #(.in_width(32), .out_width(1)) bit_extender_1 (.in(DATA_WR), .out(bit_extender_1_out));
  or or_1 (or_1_out, DOWN, RIGHT, UP);
  or or_2 (or_2_out, LEFT, RIGHT, UP);
  or or_3 (or_3_out, LEFT, DOWN, UP);
  or or_4 (or_4_out, LEFT, DOWN, RIGHT);
  Multiplexer #(.width(32)) multiplexer_2 (.in0(DATA_MEM), .in1(keyboard), .out(multiplexer_2_out), .sel(and_2_out));
  and and_1 (and_1_out, comparator_1_eq, MEM_READ);
  assign bit_extender_2_out = {{28{undriven[3]}}, undriven};  // Bit_Extender bit_extender_2
  // D_Flip_Flop d_ff_1: pin names not known; wires that end beside it: LEFT, or_1_out, DOWN, d_ff_1_p4[0]
  D_Flip_Flop d_ff_2 (.Q(d_ff_1_p4[1]), .Qn(d_ff_2_qn), .preset(d_ff_1_p4[1]));  // open: D, clk, reset
  // D_Flip_Flop d_ff_3: pin names not known; wires that end beside it: RIGHT, or_3_out, UP, d_ff_2_qn
  // D_Flip_Flop d_ff_4: pin names not known; wires that end beside it: UP, or_4_out, d_ff_4_p3
  and and_2 (and_2_out, MEM_READ, comparator_2_eq);
  Comparator #(.width(16)) comparator_2 (.a(16'hfeff), .b(ADDRESS_IN), .eq(comparator_2_eq));  // open: gt, lt
  assign bit_extender_3_out = {{28{d_ff_1_p4[3]}}, d_ff_1_p4};  // Bit_Extender bit_extender_3
  Register #(.trigger("high"), .width(32)) register_1 (
    .D(bit_extender_3_out), .Q(keyboard), .clk(CLK));  // open: en, clr
  Comparator #(.width(10)) comparator_3 (.a(ADDRESS_IN[15:6]), .b(10'h3fc), .eq(comparator_3_eq));  // open: gt, lt
  Comparator #(.width(10)) comparator_4 (.a(ADDRESS_IN[15:6]), .b(10'h3fd), .eq(comparator_4_eq));  // open: gt, lt
  Comparator #(.width(10)) comparator_5 (.a(ADDRESS_IN[15:6]), .b(10'h3fe), .eq(comparator_5_eq));  // open: gt, lt
  Comparator #(.width(10)) comparator_6 (.a(ADDRESS_IN[15:6]), .b({10{1'b1}}), .eq(comparator_6_eq));  // open: gt, lt
  and and_3 (and_3_out, wr_mem, wr_mem);
  and and_4 (and_4_out, wr_mem, comparator_4_eq);
  and and_5 (and_5_out, wr_mem, comparator_5_eq);
  and and_6 (and_6_out, wr_mem, comparator_6_eq);
  matrix_wr matrix_wr_1 (
    .address(ADDRESS_IN), .wr(and_3_out), .clk(CLK), .data(bit_extender_1_out), .row0(out_11[7:0]),
    .row1(out_11[15:8]), .row2(out_12[7:0]), .row3(out_12[15:8]), .row4(out_13[7:0]), .row5(out_13[15:8]),
    .row6(out_14[7:0]), .row7(out_14[15:8]));
  matrix_wr matrix_wr_2 (
    .address(ADDRESS_IN), .wr(and_4_out), .clk(CLK), .data(bit_extender_1_out), .row0(out_16[7:0]),
    .row1(out_16[15:8]), .row2(out_17[7:0]), .row3(out_17[15:8]), .row4(out_18[7:0]), .row5(out_18[15:8]),
    .row6(out_19[7:0]), .row7(out_19[15:8]));
  matrix_wr matrix_wr_3 (
    .address(ADDRESS_IN), .wr(and_5_out), .clk(CLK), .data(bit_extender_1_out), .row0(out_20[7:0]),
    .row1(out_20[15:8]), .row2(out_21[7:0]), .row3(out_21[15:8]), .row4(out_22[7:0]), .row5(out_22[15:8]),
    .row6(out_23[7:0]), .row7(out_23[15:8]));
  matrix_wr matrix_wr_4 (
    .address(ADDRESS_IN), .wr(and_6_out), .clk(CLK), .data(bit_extender_1_out), .row0(out_24[7:0]),
    .row1(out_24[15:8]), .row2(out_25[7:0]), .row3(out_25[15:8]), .row4(out_26[7:0]), .row5(out_26[15:8]),
    .row6(out_27[7:0]), .row7(out_27[15:8]));
  // Pins of 2 and 4 bits meet at d_ff_1_p4
endmodule
